# Fritzing sketch BlinkingLED (saved by Fritzing 0.9.10b)
breadboards: 1

parts:
  C3 = Ceramic Capacitor [capacitance=1nF voltage=5V package="100 mil [THT, multilayer]"]
  U3 = 555 Timer [package="DIP8 [THT]"]
  R5 = Resistor [tolerance=±20% resistance=1k package="0805 [SMD]"]
  R6 = Resistor [tolerance=±20% resistance=10k package="0805 [SMD]"]
  R7 = Trimmer Potentiometer [maximum_resistance=1MΩ knob_status=50% power=0.5W package=THT]
  C4 = Ceramic Capacitor [capacitance=0.1mF voltage=5V package="0603 [SMD, multilayer]"]
  LED1 = LED - 5mm [color="Red (633nm)" current=0.030 package="5 mm [THT]"]
  R8 = Resistor [tolerance=±5% power=0.25 resistance=200 package=THT]

nets:
  N1: C3.0, U3.Ground, C4.1, LED1.cathode
  N2: C3.1, U3.Reset, U3.Vcc_Supply_Voltage, R5.Pin_1
  N3: U3.Trigger, U3.Threshold, R7.wiper
  N4: U3.Output, R8.Pin_0
  N5: U3.Control_Voltage, C4.0
  N6: U3.Discharge, R5.Pin_0, R6.Pin_0
  N7: R6.Pin_1, R7.leg1
  N8: LED1.anode, R8.Pin_1
