# Fritzing sketch ClockedProgramCounter (saved by Fritzing 0.9.10b)
breadboards: 1

parts:
  Cfilter = Ceramic Capacitor [capacitance=10nF voltage=5V package="100 mil [THT, multilayer]"]
  U4 = 555 Timer [package="DIP8 [THT]"]
  R9 = Resistor [tolerance=±20% resistance=1k package="0805 [SMD]"]
  R10 = Resistor [tolerance=±20% resistance=10k package="0805 [SMD]"]
  Ct = Ceramic Capacitor [capacitance=1µF voltage=5V package="0603 [SMD, multilayer]"]
  Cctl = Ceramic Capacitor [capacitance=100nF voltage=5V package="0603 [SMD, multilayer]"]
  LED2 = LED - 5mm [color="Green (555nm)" current=0.030 package="5 mm [THT]"]
  R12 = Resistor [tolerance=±5% power=0.25 resistance=470k package=THT]
  74LS1 = 74LS161 [chip_label=74LS161 package="DIP (Dual Inline) [THT]"]
  S1 = Pushbutton [package=THT]
  R14 = Resistor [tolerance=±20% resistance=10k package="0805 [SMD]"]
  Cfilter_2 = Ceramic Capacitor [capacitance=1nF voltage=5V package="100 mil [THT, multilayer]"]
  SW1 = DIP Switch 8 Position [package=dipswitch-08]
  D1 = LED_BARGRAPH_10 [package=led_bargaph_10]
  R19 = Resistor [tolerance=±20% resistance=1k package="0805 [SMD]"]
  Rpulldowns = Resistor [tolerance=±20% resistance=10k package="0805 [SMD]"]
  R21 = Resistor [tolerance=±20% resistance=10k package="0805 [SMD]"]
  R22 = Resistor [tolerance=±20% resistance=10k package="0805 [SMD]"]
  R23 = Resistor [tolerance=±20% resistance=10k package="0805 [SMD]"]
  R27 = Resistor [tolerance=±20% resistance=1k package="0805 [SMD]"]
  R28 = TRIMPOT [maximum_resistance=10kΩ knob_status=50% power=0.5W package=3386u]
  R29 = Resistor [tolerance=±20% resistance=220 package="0805 [SMD]"]
  R30 = Resistor [tolerance=±20% resistance=10k package="0805 [SMD]"]
  S2 = Pushbutton [package="[THT]"]
  R31 = Resistor [tolerance=±20% resistance=1k package="0805 [SMD]"]
  R32 = Resistor [tolerance=±20% resistance=1k package="0805 [SMD]"]

nets:
  N1: Cfilter.0, U4.Ground, LED2.cathode, S1.leg0, S2.Pin_3, S2.Pin_4
  N2: Cfilter.1, U4.Vcc_Supply_Voltage, R9.Pin_0, R30.Pin_0
  N3: U4.Trigger, Ct.1
  N4: U4.Output, R12.Pin_0, 74LS1.CLK
  N5: U4.Reset, 74LS1.VCC, R14.Pin_1, Cfilter_2.0, SW1.5, SW1.6, SW1.7, SW1.8
  N6: U4.Control_Voltage, Cctl.1
  N7: U4.Threshold, R29.Pin_0
  N8: U4.Discharge, R9.Pin_1, R10.Pin_0
  N9: R10.Pin_1, R28.WIPER
  N10: Ct.0, Cctl.0, 74LS1.GND, Cfilter_2.1, R19.Pin_0, Rpulldowns.Pin_0, R21.Pin_0, R22.Pin_0, R23.Pin_0, R27.Pin_0, R31.Pin_0, R32.Pin_0
  N11: LED2.anode, R12.Pin_1
  N12: 74LS1.-CLR, S1.leg1, R30.Pin_1
  N13: 74LS1.In_1, SW1.9, Rpulldowns.Pin_1
  N14: 74LS1.In_2, SW1.10, R22.Pin_1
  N15: 74LS1.In_3, SW1.11, R21.Pin_1
  N16: 74LS1.In_4, SW1.12, R23.Pin_1
  N17: 74LS1.ENP, 74LS1.-LOAD, 74LS1.ENT, R14.Pin_0, S2.Pin_1, S2.Pin_2
  N18: 74LS1.Out_4, D1.G_A
  N19: 74LS1.Out_3, D1.H_A
  N20: 74LS1.Out_2, D1.I_A
  N21: 74LS1.Out_1, D1.J_A
  N22: D1.J_C, R19.Pin_1
  N23: D1.I_C, R27.Pin_1
  N24: D1.H_C, R31.Pin_1
  N25: D1.G_C, R32.Pin_1
  N26: R28.CW, R29.Pin_1

custom parts:
  74LS161: 74LS161 synchronous counter with asynchronous clear
