// Logisim project MiniALU.circ as structural Verilog: 2 circuits, main circuit main
module main (
);

  wire adder_1_cout, AddOp, and_1_out, and_2_out, and_3_out, clockOut, comparator_1_eq, comparator_1_gt,
       comparator_1_lt, decoder_1_out1, decoder_1_out2, demultiplexer_2_out4, demultiplexer_2_out6,
       demultiplexer_2_out7, demultiplexer_2_out8, EqOp, GTOp, LTOp, n74161_1_pin1, n74161_1_pin7, NEQOp,
       or_3_out, or_5_out, or_6_out, SubOp, t_ff_1_q, t_ff_1_qn, t_ff_2_q, t_ff_2_qn, t_ff_3_q, t_ff_3_qn,
       t_ff_4_qn, xor_1_out;
  wire [3:0] ALUResult_q, ALUResult_q_2, n74161_1_pin14, OpcodeHB, OpcodeLB, RIP_q;
  wire [7:0] addResult, and_4_out, and_5_out, bit_extender_1_out, compResult, or_4_out, ValB, ValC,
       willDisplayAdd, willDisplayComp, xor_2_out;
  wire [23:16] rom_1_data;

  Clock clock_1 (.out(clockOut));
  T_Flip_Flop t_ff_1 (.T(clockOut), .clk(clockOut), .Q(t_ff_1_q), .Qn(t_ff_1_qn));  // open: reset, preset
  _74161 u_74161_1 (
    .pin1(n74161_1_pin1), .pin2(clockOut), .pin7(n74161_1_pin7), .pin14(n74161_1_pin14[0]),
    .pin13(n74161_1_pin14[1]), .pin12(n74161_1_pin14[2]), .pin11(n74161_1_pin14[3]), .pin10(n74161_1_pin7),
    .pin9(n74161_1_pin7));  // open: pin3, pin4, pin5, pin6, pin15
  T_Flip_Flop t_ff_2 (.T(t_ff_1_q), .clk(t_ff_1_q), .Q(t_ff_2_q), .Qn(t_ff_2_qn));  // open: reset, preset
  T_Flip_Flop t_ff_3 (.T(t_ff_2_q), .clk(t_ff_2_q), .Q(t_ff_3_q), .Qn(t_ff_3_qn));  // open: reset, preset
  T_Flip_Flop t_ff_4 (.T(t_ff_3_q), .clk(t_ff_3_q), .Qn(t_ff_4_qn));  // open: Q, reset, preset
  ROM #(.addrWidth(4), .dataWidth(32)) rom_1 (.addr(RIP_q), .data({OpcodeHB, OpcodeLB, rom_1_data, ValB, ValC}));
  Register #(.width(4)) RIP (.D(n74161_1_pin14), .en(n74161_1_pin7), .Q(RIP_q), .clk(clockOut));  // open: clr
  Decoder #(.enable("false"), .select(4)) decoder_1 (
    .out1(decoder_1_out1), .out2(decoder_1_out2), .sel(OpcodeHB));  // open: out0, out3, out4, out5, out6, out7, out8, out9, out10, out11, out12, out13, out14, out15
  Demultiplexer #(.select(4)) demultiplexer_1 (
    .out0(AddOp), .out1(SubOp), .in(decoder_1_out1), .sel(OpcodeLB));  // open: out2, out3, out4, out5, out6, out7, out8, out9, out10, out11, out12, out13, out14, out15
  Demultiplexer #(.select(4)) demultiplexer_2 (
    .out4(demultiplexer_2_out4), .out5(NEQOp), .out6(demultiplexer_2_out6), .out7(demultiplexer_2_out7),
    .out8(demultiplexer_2_out8), .out9(LTOp), .in(decoder_1_out2), .sel(OpcodeLB));  // open: out0, out1, out2, out3, out10, out11, out12, out13, out14, out15
  or or_1 (EqOp, demultiplexer_2_out4, NEQOp, demultiplexer_2_out6, demultiplexer_2_out7);
  or or_2 (GTOp, demultiplexer_2_out6, demultiplexer_2_out8);
  and and_1 (and_1_out, GTOp, comparator_1_gt);
  Comparator comparator_1 (.a(ValB), .b(ValC), .gt(comparator_1_gt), .eq(comparator_1_eq), .lt(comparator_1_lt));
  and and_2 (and_2_out, comparator_1_lt, LTOp);
  assign bit_extender_1_out = {{7{SubOp}}, SubOp};  // Bit_Extender bit_extender_1
  xor xor_1 (xor_1_out, NEQOp, comparator_1_eq);
  Adder adder_1 (.a(ValB), .b(xor_2_out), .out(addResult), .cin(SubOp), .cout(adder_1_cout));
  assign xor_2_out = ValC ^ bit_extender_1_out;  // XOR_Gate xor_2, 8 bits wide
  LED CarryOut (.in(adder_1_cout));
  and and_3 (and_3_out, EqOp, xor_1_out);
  or or_3 (or_3_out, and_1_out, and_3_out, and_2_out);
  assign compResult = {{7{or_3_out}}, or_3_out};  // Bit_Extender bit_extender_2
  Hex_Digit_Display hex_digit_display_1 (.value(ALUResult_q_2));  // open: dp
  assign or_4_out = and_4_out | and_5_out;  // OR_Gate or_4, 8 bits wide
  assign and_4_out = compResult & willDisplayComp;  // AND_Gate and_4, 8 bits wide
  assign and_5_out = addResult & willDisplayAdd;  // AND_Gate and_5, 8 bits wide
  assign willDisplayAdd = {{7{or_5_out}}, or_5_out};  // Bit_Extender bit_extender_3
  or or_5 (or_5_out, SubOp, AddOp);
  assign willDisplayComp = {{7{or_6_out}}, or_6_out};  // Bit_Extender bit_extender_4
  or or_6 (or_6_out, EqOp, NEQOp, GTOp, LTOp);
  Hex_Digit_Display hex_digit_display_2 (.value(ALUResult_q));  // open: dp
  Register ALUResult (.D(or_4_out), .Q({ALUResult_q_2, ALUResult_q}), .clk(clockOut));  // open: en, clr
  // also tied to VCC on the sheet: {n74161_1_pin1, n74161_1_pin7}

  // Notes on the sheet:
  //   contents of rom_1 (hex, n*v repeats v):
  //   10ff0102 11ff0803 10ffff01 24ff4a4a 28ff0201 24ff00ff 28ff0102 26ff0301
endmodule

module registerTest (
  input  [7:0] in_1,
  input  [7:0] in_2,
  input  [7:0] in_3,
  input  [7:0] in_4,
  input  [7:0] in_5,
  input  [7:0] in_6,
  input  [7:0] in_7,
  input  [7:0] in_8,
  input  useRC,
  input  useRB,
  input  useRA,
  input  enableLoad_activeLow
);

  wire clock_1_out, n74161_1_pin1;
  wire [2:0] rom_1_data, rom_1_data_3, rom_1_data_4;
  wire [3:0] and_1_out, bit_extender_1_out, dipswitch_1_sw4, n74161_1_pin14, OpcodeHB, OpcodeLB, or_1_out,
       register_1_q;
  wire [7:0] and_2_out, and_3_out, and_4_out, bit_extender_2_out, bit_extender_3_out, bit_extender_4_out,
       multiplexer_1_out, multiplexer_2_out, multiplexer_3_out, R0_q, R1_q, R2_q, R3_q, R4_q, R5_q, R6_q,
       R7_q;
  wire [23:3] rom_1_data_2;

  Clock clock_1 (.out(clock_1_out));
  _74161 u_74161_1 (
    .pin1(n74161_1_pin1), .pin2(clock_1_out), .pin7(enableLoad_activeLow), .pin14(n74161_1_pin14[0]),
    .pin13(n74161_1_pin14[1]), .pin12(n74161_1_pin14[2]), .pin11(n74161_1_pin14[3]),
    .pin10(enableLoad_activeLow), .pin9(enableLoad_activeLow));  // open: pin3, pin4, pin5, pin6, pin15
  assign bit_extender_1_out = {{3{enableLoad_activeLow}}, enableLoad_activeLow};  // Bit_Extender bit_extender_1
  assign and_1_out = bit_extender_1_out & dipswitch_1_sw4;  // AND_Gate and_1, 4 bits wide
  DipSwitch #(.number(4)) dipswitch_1 (
    .sw1(dipswitch_1_sw4[3]), .sw2(dipswitch_1_sw4[2]), .sw3(dipswitch_1_sw4[1]), .sw4(dipswitch_1_sw4[0]));
  assign or_1_out = n74161_1_pin14 | and_1_out;  // OR_Gate or_1, 4 bits wide
  ROM #(.addrWidth(4), .dataWidth(32)) rom_1 (
    .addr(register_1_q),
    .data({OpcodeHB, OpcodeLB, rom_1_data_2[23:19], rom_1_data_4, rom_1_data_2[15:11], rom_1_data_3, rom_1_data_2[7:3], rom_1_data}));
  Register #(.width(4)) register_1 (.D(or_1_out), .en(clock_1_out), .Q(register_1_q), .clk(clock_1_out));  // open: clr
  Register R7 (.D(in_8), .en(clock_1_out), .Q(R7_q), .clk(clock_1_out));  // open: clr
  Register R6 (.D(in_7), .en(clock_1_out), .Q(R6_q), .clk(clock_1_out));  // open: clr
  Register R5 (.D(in_6), .en(clock_1_out), .Q(R5_q), .clk(clock_1_out));  // open: clr
  Register R4 (.D(in_5), .en(clock_1_out), .Q(R4_q), .clk(clock_1_out));  // open: clr
  Register R3 (.D(in_4), .en(clock_1_out), .Q(R3_q), .clk(clock_1_out));  // open: clr
  Register R2 (.D(in_3), .en(clock_1_out), .Q(R2_q), .clk(clock_1_out));  // open: clr
  Register R1 (.D(in_2), .en(clock_1_out), .Q(R1_q), .clk(clock_1_out));  // open: clr
  Register R0 (.D(in_1), .en(clock_1_out), .Q(R0_q), .clk(clock_1_out));  // open: clr
  Multiplexer #(.select(3), .width(8)) multiplexer_1 (
    .in0(R0_q), .in1(R1_q), .in2(R2_q), .in3(R3_q), .in4(R4_q), .in5(R5_q), .in6(R6_q), .in7(R7_q),
    .out(multiplexer_1_out), .sel(rom_1_data));
  Multiplexer #(.select(3), .width(8)) multiplexer_2 (
    .in0(R0_q), .in1(R1_q), .in2(R2_q), .in3(R3_q), .in4(R4_q), .in5(R5_q), .in6(R6_q), .in7(R7_q),
    .out(multiplexer_2_out), .sel(rom_1_data_3));
  Multiplexer #(.select(3), .width(8)) multiplexer_3 (
    .in0(R0_q), .in1(R1_q), .in2(R2_q), .in3(R3_q), .in4(R4_q), .in5(R5_q), .in6(R6_q), .in7(R7_q),
    .out(multiplexer_3_out), .sel(rom_1_data_4));
  assign bit_extender_2_out = {{7{useRC}}, useRC};  // Bit_Extender bit_extender_2
  assign and_2_out = bit_extender_2_out & multiplexer_1_out;  // AND_Gate and_2, 8 bits wide
  assign bit_extender_3_out = {{7{useRB}}, useRB};  // Bit_Extender bit_extender_3
  assign and_3_out = bit_extender_3_out & multiplexer_2_out;  // AND_Gate and_3, 8 bits wide
  assign bit_extender_4_out = {{7{useRA}}, useRA};  // Bit_Extender bit_extender_4
  assign and_4_out = bit_extender_4_out & multiplexer_3_out;  // AND_Gate and_4, 8 bits wide
  Hex_Digit_Display hex_digit_display_1 (.value(and_2_out[3:0]));  // open: dp
  Hex_Digit_Display hex_digit_display_2 (.value(and_3_out[3:0]));  // open: dp
  Hex_Digit_Display hex_digit_display_3 (.value(and_4_out[3:0]));  // open: dp
  // also tied to VCC on the sheet: n74161_1_pin1

  // Notes on the sheet:
  //   contents of rom_1 (hex, n*v repeats v):
  //   0 1 102 10203 1020304 2030405 3040506 4050607 5060700 6070000 7000000 1010101 2020202 3030303
  //   4040404 5050505
endmodule
